// Logisim project regfile.circ as structural Verilog: 1 circuit, main circuit main
module main (
  input  [4:0] Read_Register_1,
  input  [4:0] Read_Register_2,
  input  [4:0] Write_Register,
  input  [31:0] Write_Data,
  input  in_5,
  input  Write_Enable,
  input  Clock,
  output [31:0] s0_Value,
  output [31:0] s1_Value,
  output [31:0] s2_Value,
  output [31:0] ra_Value,
  output [31:0] Read_Data_1,
  output [31:0] Read_Data_2
);

  wire demultiplexer_1_out1, demultiplexer_1_out2, demultiplexer_1_out3, demultiplexer_1_out4,
       demultiplexer_1_out5, demultiplexer_1_out6, demultiplexer_1_out7, demultiplexer_1_out8,
       demultiplexer_1_out9, demultiplexer_1_out10, demultiplexer_1_out11, demultiplexer_1_out12,
       demultiplexer_1_out13, demultiplexer_1_out14, demultiplexer_1_out15, demultiplexer_1_out16,
       demultiplexer_1_out17, demultiplexer_1_out18, demultiplexer_1_out19, demultiplexer_1_out20,
       demultiplexer_1_out21, demultiplexer_1_out22, demultiplexer_1_out23, demultiplexer_1_out24,
       demultiplexer_1_out25, demultiplexer_1_out26, demultiplexer_1_out27, demultiplexer_1_out28,
       demultiplexer_1_out29, demultiplexer_1_out30, demultiplexer_1_out31;
  wire [31:0] _0, a0, a1, a2, a3, at, fp, gp, k0, k1, s3, s4, s5, s6, s7, sp, t0, t1, t2, t3, t4, t5, t6, t7,
       t8, t9, v0, v1;

  Demultiplexer #(.select(5)) demultiplexer_1 (
    .out1(demultiplexer_1_out1), .out2(demultiplexer_1_out2), .out3(demultiplexer_1_out3),
    .out4(demultiplexer_1_out4), .out5(demultiplexer_1_out5), .out6(demultiplexer_1_out6),
    .out7(demultiplexer_1_out7), .out8(demultiplexer_1_out8), .out9(demultiplexer_1_out9),
    .out10(demultiplexer_1_out10), .out11(demultiplexer_1_out11), .out12(demultiplexer_1_out12),
    .out13(demultiplexer_1_out13), .out14(demultiplexer_1_out14), .out15(demultiplexer_1_out15),
    .out16(demultiplexer_1_out16), .out17(demultiplexer_1_out17), .out18(demultiplexer_1_out18),
    .out19(demultiplexer_1_out19), .out20(demultiplexer_1_out20), .out21(demultiplexer_1_out21),
    .out22(demultiplexer_1_out22), .out23(demultiplexer_1_out23), .out24(demultiplexer_1_out24),
    .out25(demultiplexer_1_out25), .out26(demultiplexer_1_out26), .out27(demultiplexer_1_out27),
    .out28(demultiplexer_1_out28), .out29(demultiplexer_1_out29), .out30(demultiplexer_1_out30),
    .out31(demultiplexer_1_out31), .in(Write_Enable), .sel(Write_Register));  // open: out0, en
  Register #(.width(32)) u__0 (.en(in_5), .Q(_0), .clk(Clock));  // open: D, clr
  Register #(.width(32)) u_at (.D(Write_Data), .en(demultiplexer_1_out1), .Q(at), .clk(Clock));  // open: clr
  Register #(.width(32)) u_v0 (.D(Write_Data), .en(demultiplexer_1_out2), .Q(v0), .clk(Clock));  // open: clr
  Register #(.width(32)) u_v1 (.D(Write_Data), .en(demultiplexer_1_out3), .Q(v1), .clk(Clock));  // open: clr
  Register #(.width(32)) u_a0 (.D(Write_Data), .en(demultiplexer_1_out4), .Q(a0), .clk(Clock));  // open: clr
  Register #(.width(32)) u_a1 (.D(Write_Data), .en(demultiplexer_1_out5), .Q(a1), .clk(Clock));  // open: clr
  Register #(.width(32)) u_a2 (.D(Write_Data), .en(demultiplexer_1_out6), .Q(a2), .clk(Clock));  // open: clr
  Register #(.width(32)) u_a3 (.D(Write_Data), .en(demultiplexer_1_out7), .Q(a3), .clk(Clock));  // open: clr
  Register #(.width(32)) u_t0 (.D(Write_Data), .en(demultiplexer_1_out8), .Q(t0), .clk(Clock));  // open: clr
  Register #(.width(32)) u_t1 (.D(Write_Data), .en(demultiplexer_1_out9), .Q(t1), .clk(Clock));  // open: clr
  Register #(.width(32)) u_t2 (.D(Write_Data), .en(demultiplexer_1_out10), .Q(t2), .clk(Clock));  // open: clr
  Register #(.width(32)) u_t3 (.D(Write_Data), .en(demultiplexer_1_out11), .Q(t3), .clk(Clock));  // open: clr
  Register #(.width(32)) u_t4 (.D(Write_Data), .en(demultiplexer_1_out12), .Q(t4), .clk(Clock));  // open: clr
  Register #(.width(32)) u_t5 (.D(Write_Data), .en(demultiplexer_1_out13), .Q(t5), .clk(Clock));  // open: clr
  Register #(.width(32)) u_t6 (.D(Write_Data), .en(demultiplexer_1_out14), .Q(t6), .clk(Clock));  // open: clr
  Register #(.width(32)) u_t7 (.D(Write_Data), .en(demultiplexer_1_out15), .Q(t7), .clk(Clock));  // open: clr
  Register #(.width(32)) s0 (.D(Write_Data), .en(demultiplexer_1_out16), .Q(s0_Value), .clk(Clock));  // open: clr
  Register #(.width(32)) s1 (.D(Write_Data), .en(demultiplexer_1_out17), .Q(s1_Value), .clk(Clock));  // open: clr
  Register #(.width(32)) s2 (.D(Write_Data), .en(demultiplexer_1_out18), .Q(s2_Value), .clk(Clock));  // open: clr
  Register #(.width(32)) u_s3 (.D(Write_Data), .en(demultiplexer_1_out19), .Q(s3), .clk(Clock));  // open: clr
  Register #(.width(32)) u_s4 (.D(Write_Data), .en(demultiplexer_1_out20), .Q(s4), .clk(Clock));  // open: clr
  Register #(.width(32)) u_s5 (.D(Write_Data), .en(demultiplexer_1_out21), .Q(s5), .clk(Clock));  // open: clr
  Register #(.width(32)) u_s6 (.D(Write_Data), .en(demultiplexer_1_out22), .Q(s6), .clk(Clock));  // open: clr
  Register #(.width(32)) u_s7 (.D(Write_Data), .en(demultiplexer_1_out23), .Q(s7), .clk(Clock));  // open: clr
  Register #(.width(32)) u_t8 (.D(Write_Data), .en(demultiplexer_1_out24), .Q(t8), .clk(Clock));  // open: clr
  Register #(.width(32)) u_t9 (.D(Write_Data), .en(demultiplexer_1_out25), .Q(t9), .clk(Clock));  // open: clr
  Register #(.width(32)) u_k0 (.D(Write_Data), .en(demultiplexer_1_out26), .Q(k0), .clk(Clock));  // open: clr
  Register #(.width(32)) u_k1 (.D(Write_Data), .en(demultiplexer_1_out27), .Q(k1), .clk(Clock));  // open: clr
  Register #(.width(32)) u_gp (.D(Write_Data), .en(demultiplexer_1_out28), .Q(gp), .clk(Clock));  // open: clr
  Register #(.width(32)) u_sp (.D(Write_Data), .en(demultiplexer_1_out29), .Q(sp), .clk(Clock));  // open: clr
  Register #(.width(32)) u_fp (.D(Write_Data), .en(demultiplexer_1_out30), .Q(fp), .clk(Clock));  // open: clr
  Register #(.width(32)) ra (.D(Write_Data), .en(demultiplexer_1_out31), .Q(ra_Value), .clk(Clock));  // open: clr
  Multiplexer #(.select(5), .width(32)) multiplexer_1 (
    .in0(_0), .in1(at), .in2(v0), .in3(v1), .in4(a0), .in5(a1), .in6(a2), .in7(a3), .in8(t0), .in9(t1),
    .in10(t2), .in11(t3), .in12(t4), .in13(t5), .in14(t6), .in15(t7), .in16(s0_Value), .in17(s1_Value),
    .in18(s2_Value), .in19(s3), .in20(s4), .in21(s5), .in22(s6), .in23(s7), .in24(t8), .in25(t9), .in26(k0),
    .in27(k1), .in28(gp), .in29(sp), .in30(fp), .in31(ra_Value), .out(Read_Data_1), .sel(Read_Register_1));  // open: en
  Multiplexer #(.select(5), .width(32)) multiplexer_2 (
    .in0(_0), .in1(at), .in2(v0), .in3(v1), .in4(a0), .in5(a1), .in6(a2), .in7(a3), .in8(t0), .in9(t1),
    .in10(t2), .in11(t3), .in12(t4), .in13(t5), .in14(t6), .in15(t7), .in16(s0_Value), .in17(s1_Value),
    .in18(s2_Value), .in19(s3), .in20(s4), .in21(s5), .in22(s6), .in23(s7), .in24(t8), .in25(t9), .in26(k0),
    .in27(k1), .in28(gp), .in29(sp), .in30(fp), .in31(ra_Value), .out(Read_Data_2), .sel(Read_Register_2));  // open: en

  // Other names for the same wires on the sheet: clk = Clock; ra[31:0] = ra_Value; read_data1[31:0] = Read_Data_1;
  //   read_data2[31:0] = Read_Data_2; read_reg1[4:0] = Read_Register_1; read_reg2[4:0] = Read_Register_2;
  //   s0[31:0] = s0_Value; s1[31:0] = s1_Value; s2[31:0] = s2_Value; write_en = Write_Enable;
  //   write_reg[4:0] = Write_Register

  // Notes on the sheet:
  //   INPUTS to your circuit
  //   DON'T CHANGE THE LOCATIONS OF THE INPUTS AND OUTPUTS!
  //   These are DEBUG/TEST outputs from your circuit.
  //   OUTPUTS from your circuit
endmodule
